# Fritzing sketch Proyecto1 (saved by Fritzing 0.9.3b)

parts:
  U1 = atmega328 [package=dip]
  C1 = Capacitor [package=cap-pth-small2]
  C2 = Capacitor [package=cap-pth-small2]
  IC1 = L293D [package=THT]
  VCC1 = Battery
  hc-sr1 = hc-sr04
  U2 = Vibration Motor- ROB-08449 [package=vibe-motor-10mm]
  R2 = Resistor [tolerance=±5% resistance=220 package="0603 [SMD]"]
  XTAL2 = Crystal [frequency="16 Mhz" package=THT]

nets (from the breadboard view):
  N1: U1.RESET, R2.Pin_1
  VCC: U1.VCC, VCC1.+, hc-sr1.VCC, R2.Pin_0
  GND: U1.GND, C1.1, C2.1, IC1.0V, VCC1.-, hc-sr1.GND
  N2: U1.XLAT1, C1.2, XTAL2.pin_0
  N3: U1.XLAT2, C2.2, XTAL2.pin_1
  N4: U1.D9_(PWM), IC1.Enable_1
  N5: U1.D10_(PWM), IC1.In_1
  N6: U1.D11_(PWM), IC1.In_2
  N7: U1.D12, hc-sr1.Echo
  N8: U1.D13, hc-sr1.Trig
  N9: U1.AVCC, IC1.+Vmotor
  N10: IC1.Out_1_(_Controlled_by_Enable_1_), U2.+
  N11: IC1.Out_2_(_Controlled_by_Enable_1_), U2.-
